// Logisim project TuringMachine.circ as structural Verilog: 4 circuits, main circuit main
module main (
);

  wire and_1_out, Clock, clock_1_out, Comparador__1_si_iguales, controlled_buffer_4_out,
       controlled_buffer_6_out, counter_1_carry, Etapa_0, Etapa_1, Etapa_2, Etapa_3, Etapa_4, not_1_out,
       not_2_out, or_1_out;
  wire [2:0] counter_2_q;
  wire [6:0] \Carácter_Actual_q , controlled_buffer_2_out, controlled_buffer_3_out, MBR;
  wire [7:0] counter_1_q, register_1_q;
  wire [9:0] controlled_buffer_7_out, Current_Position_q, Direction_Control_displaced_location, register_2_q;
  wire [31:0] rom_1_data;

  and and_1 (and_1_out, Etapa_1, ~Comparador__1_si_iguales);  // AND_Gate
  Clock clock_1 (.out(clock_1_out));
  not not_1 (not_1_out, counter_1_carry);
  Counter counter_1 (
    .count(and_1_out), .Q(counter_1_q), .carry(counter_1_carry), .clk(Clock), .clr(Etapa_0));  // open: load, D, preset, down
  assign Clock = not_1_out ? clock_1_out : 1'bz;  // Controlled_Buffer controlled_buffer_1
  ROM #(.dataWidth(32)) rom_1 (.addr(counter_1_q), .data(rom_1_data));
  assign controlled_buffer_2_out = Etapa_0 ? MBR : 7'bz;  // Controlled_Buffer controlled_buffer_2
  assign controlled_buffer_3_out = Etapa_2 ? rom_1_data[15:9] : 7'bz;  // Controlled_Buffer controlled_buffer_3
  Register #(.width(7)) \Carácter_Actual  (
    .D(controlled_buffer_2_out), .en(Etapa_0), .Q(\Carácter_Actual_q ), .clk(Clock));  // open: clr
  Register register_1 (.D(rom_1_data[7:0]), .en(Etapa_4), .Q(register_1_q), .clk(Clock));  // open: clr
  assign controlled_buffer_4_out = Etapa_2 ? Clock : 1'bz;  // Controlled_Buffer controlled_buffer_4
  assign MBR = Etapa_2 ? controlled_buffer_3_out : 7'bz;  // Controlled_Buffer controlled_buffer_5
  Comparador Comparador (
    .Caracter1(\Carácter_Actual_q ), .Caracter2(rom_1_data[22:16]), .Estado1(register_1_q),
    .Estado2(rom_1_data[30:23]), ._1_si_iguales(Comparador__1_si_iguales));
  not not_2 (not_2_out, Etapa_2);
  or or_1 (or_1_out, Comparador__1_si_iguales, ~Etapa_1);  // OR_Gate
  Counter #(.width(3), .max('h4)) counter_2 (
    .count(or_1_out), .Q(counter_2_q), .clk(Clock));  // open: load, D, carry, clr, preset, down
  RAM #(.addrWidth(10), .dataWidth(7)) ram_1 (
    .addr(Current_Position_q), .data(MBR), .clk(controlled_buffer_4_out), .ld(not_2_out));  // open: sel, clr
  Decoder #(.select(3), .enable("false")) decoder_1 (
    .out0(Etapa_0), .out1(Etapa_1), .out2(Etapa_2), .out3(Etapa_3), .out4(Etapa_4), .sel(counter_2_q));  // open: out5, out6, out7
  assign controlled_buffer_6_out = Etapa_4 ? rom_1_data[8] : 1'bz;  // Controlled_Buffer controlled_buffer_6
  \OperadordeDirección  Direction_Control (
    .Current_Memory_Address(register_2_q), .Left_Right_Switch(controlled_buffer_6_out),
    .Displaced_Location(Direction_Control_displaced_location));
  Register #(.width(10)) register_2 (.D(controlled_buffer_7_out), .Q(register_2_q), .clk(Clock));  // open: en, clr
  assign controlled_buffer_7_out = Etapa_3 ? Current_Position_q : 10'bz;  // Controlled_Buffer controlled_buffer_7
  Register #(.width(10)) Current_Position (
    .D(Direction_Control_displaced_location), .en(Etapa_4), .Q(Current_Position_q), .clk(Clock));  // open: clr

  // Notes on the sheet:
  //   contents of rom_1 (hex, n*v repeats v):
  //   f0 102f1 7fff33 78000000 78010203 787fff33 8000f1 8102f3 ffffe7 78800001 78810200 78ffffe7 18000f3
  //   18102f0 1ffffe7 79800003 79810201 79ffffe7 19800133 19810333 19ff1faa 738001e7 738103e7 73ff07aa
endmodule

module RAMEL (
  input  [6:0] Store_Data,
  input  [9:0] MAR,
  input  Input_Output_switch,
  input  Clock,
  output [6:0] Stored_Loaded_Data
);

  wire not_1_out;

  assign Stored_Loaded_Data = Input_Output_switch ? Store_Data : 7'bz;  // Controlled_Buffer controlled_buffer_1
  not not_1 (not_1_out, Input_Output_switch);
  RAM #(.addrWidth(10), .dataWidth(7)) ram_1 (
    .addr(MAR), .data(Stored_Loaded_Data), .clk(Clock), .ld(not_1_out));  // open: sel, clr
endmodule

module \OperadordeDirección  (
  input  [9:0] Current_Memory_Address,
  input  Left_Right_Switch,
  output [9:0] Displaced_Location
);

  wire not_1_out;
  wire [9:0] adder_1_out, subtractor_1_out;

  Subtractor #(.width(10)) subtractor_1 (
    .a(Current_Memory_Address), .b(10'h1), .out(subtractor_1_out));  // open: bin, bout
  Adder #(.width(10)) adder_1 (.a(Current_Memory_Address), .b(10'h1), .out(adder_1_out));  // open: cin, cout
  assign Displaced_Location = Left_Right_Switch ? adder_1_out : 10'bz;  // Controlled_Buffer controlled_buffer_1
  not not_1 (not_1_out, Left_Right_Switch);
  assign Displaced_Location = not_1_out ? subtractor_1_out : 10'bz;  // Controlled_Buffer controlled_buffer_2
endmodule

module Comparador (
  input  [6:0] Caracter1,
  input  [6:0] Caracter2,
  input  [7:0] Estado1,
  input  [7:0] Estado2,
  output _1_si_iguales
);

  wire comparator_1_eq, comparator_2_eq;

  Comparator #(.width(7)) comparator_1 (.a(Caracter1), .b(Caracter2), .eq(comparator_1_eq));  // open: gt, lt
  Comparator comparator_2 (.a(Estado1), .b(Estado2), .eq(comparator_2_eq));  // open: gt, lt
  and and_1 (_1_si_iguales, comparator_1_eq, comparator_2_eq);
endmodule
